// Logisim project 7SegmentDecoder.circ as structural Verilog: 9 circuits, main circuit main
module main (
  input  D,
  input  C,
  input  B,
  input  A
);

  wire binaryto7segmentdecoder_1_sa, binaryto7segmentdecoder_1_sb, binaryto7segmentdecoder_1_sc,
       binaryto7segmentdecoder_1_sd, binaryto7segmentdecoder_1_se, binaryto7segmentdecoder_1_sf,
       binaryto7segmentdecoder_1_sg;

  BinaryTo7SegmentDecoder binaryto7segmentdecoder_1 (
    .D(D), .C(C), .B(B), .A(A), .sA(binaryto7segmentdecoder_1_sa), .sB(binaryto7segmentdecoder_1_sb),
    .sC(binaryto7segmentdecoder_1_sc), .sD(binaryto7segmentdecoder_1_sd), .sE(binaryto7segmentdecoder_1_se),
    .sF(binaryto7segmentdecoder_1_sf), .sG(binaryto7segmentdecoder_1_sg));
  _7_Segment_Display u_7_segment_display_1 (
    .g(binaryto7segmentdecoder_1_sg), .f(binaryto7segmentdecoder_1_sf), .a(binaryto7segmentdecoder_1_sa),
    .b(binaryto7segmentdecoder_1_sb), .e(binaryto7segmentdecoder_1_se), .d(binaryto7segmentdecoder_1_sd),
    .c(binaryto7segmentdecoder_1_sc));  // open: dp
endmodule

module BinaryTo_7Segment_a (
  input  D,
  input  C,
  input  B,
  input  A,
  output Sa
);

  wire and_1_out, and_2_out, and_3_out, and_4_out, not_1_out, not_2_out, not_3_out, not_4_out, not_5_out,
       not_6_out, not_7_out;

  not not_1 (not_1_out, D);
  not not_2 (not_2_out, C);
  not not_3 (not_3_out, B);
  not not_4 (not_4_out, D);
  not not_5 (not_5_out, C);
  not not_6 (not_6_out, B);
  not not_7 (not_7_out, A);
  and and_1 (and_1_out, not_1_out, B);
  and and_2 (and_2_out, D, not_2_out, not_3_out);
  and and_3 (and_3_out, not_4_out, C, A);
  and and_4 (and_4_out, not_5_out, not_6_out, not_7_out);
  or or_1 (Sa, and_1_out, and_2_out, and_3_out, and_4_out);
endmodule

module BinaryTo_7Segment_b (
  input  D,
  input  C,
  input  B,
  input  A,
  output Sa
);

  wire and_1_out, and_2_out, and_3_out, and_4_out, not_1_out, not_2_out, not_3_out, not_4_out;

  not not_1 (not_1_out, D);
  not not_2 (not_2_out, C);
  not not_3 (not_3_out, B);
  not not_4 (not_4_out, A);
  and and_1 (and_1_out, not_1_out, not_2_out, not_4_out);
  and and_2 (and_2_out, not_1_out, B, A);
  and and_3 (and_3_out, not_1_out, not_3_out, not_4_out);
  and and_4 (and_4_out, not_2_out, not_3_out);
  or or_1 (Sa, and_1_out, and_2_out, and_3_out, and_4_out);
endmodule

module BinaryTo_7Segment_c (
  input  D,
  input  C,
  input  B,
  input  A,
  output Sa
);

  wire not_1_out;

  not not_1 (not_1_out, B);
  or or_1 (Sa, D, C, not_1_out, A);
endmodule

module BinaryTo_7Segment_d (
  input  D,
  input  C,
  input  B,
  input  A,
  output Sa
);

  wire not_1_out, not_2_out, not_3_out, or_1_out, or_2_out, or_3_out;

  not not_1 (not_1_out, C);
  not not_2 (not_2_out, B);
  not not_3 (not_3_out, A);
  or or_1 (or_1_out, D, C, B, not_3_out);
  or or_2 (or_2_out, D, not_1_out, B, A);
  or or_3 (or_3_out, D, not_1_out, not_2_out, not_3_out);
  and and_1 (Sa, or_1_out, or_2_out, or_3_out);
endmodule

module BinaryTo_7Segment_e (
  input  D,
  input  C,
  input  B,
  input  A,
  output Sa
);

  wire and_1_out, and_2_out, not_1_out, not_2_out, not_3_out, not_4_out, or_1_out;

  not not_1 (not_1_out, D);
  not not_2 (not_2_out, C);
  not not_3 (not_3_out, B);
  not not_4 (not_4_out, A);
  and and_1 (and_1_out, not_2_out, not_3_out);
  and and_2 (and_2_out, not_1_out, B);
  or or_1 (or_1_out, and_1_out, and_2_out);
  and and_3 (Sa, not_4_out, or_1_out);
endmodule

module BinaryTo_7Segment_f (
  input  D,
  input  C,
  input  B,
  input  A,
  output Sa
);

  wire not_1_out, not_2_out, not_3_out, or_1_out, or_2_out, or_3_out, or_4_out;

  not not_1 (not_1_out, C);
  not not_2 (not_2_out, B);
  not not_3 (not_3_out, A);
  or or_1 (or_1_out, D, C, B, not_3_out);
  or or_2 (or_2_out, D, C, not_2_out, A);
  or or_3 (or_3_out, D, C, not_2_out, not_3_out);
  or or_4 (or_4_out, D, not_1_out, not_2_out, not_3_out);
  and and_1 (Sa, or_1_out, or_2_out, or_3_out, or_4_out);
endmodule

module BinaryTo_7Segment_g (
  input  D,
  input  C,
  input  B,
  input  A,
  output Sa
);

  wire not_1_out, not_2_out, not_3_out, or_1_out, or_2_out, or_3_out;

  not not_1 (not_1_out, C);
  not not_2 (not_2_out, B);
  not not_3 (not_3_out, A);
  or or_1 (or_1_out, D, C, B, A);
  or or_2 (or_2_out, D, C, B, not_3_out);
  or or_3 (or_3_out, D, not_1_out, not_2_out, not_3_out);
  and and_1 (Sa, or_1_out, or_2_out, or_3_out);
endmodule

module BinaryTo7SegmentDecoder (
  input  D,
  input  C,
  input  B,
  input  A,
  output sA,
  output sB,
  output sC,
  output sD,
  output sE,
  output sF,
  output sG
);

  BinaryTo_7Segment_a binaryto_7segment_a_1 (.D(D), .C(C), .B(B), .A(A), .Sa(sA));
  BinaryTo_7Segment_b binaryto_7segment_b_1 (.D(D), .C(C), .B(B), .A(A), .Sa(sB));
  BinaryTo_7Segment_c binaryto_7segment_c_1 (.D(D), .C(C), .B(B), .A(A), .Sa(sC));
  BinaryTo_7Segment_d binaryto_7segment_d_1 (.D(D), .C(C), .B(B), .A(A), .Sa(sD));
  BinaryTo_7Segment_e binaryto_7segment_e_1 (.D(D), .C(C), .B(B), .A(A), .Sa(sE));
  BinaryTo_7Segment_f binaryto_7segment_f_1 (.D(D), .C(C), .B(B), .A(A), .Sa(sF));
  BinaryTo_7Segment_g binaryto_7segment_g_1 (.D(D), .C(C), .B(B), .A(A), .Sa(sG));
endmodule
